# Fritzing sketch poseur-blocks-schematic (saved by Fritzing 0.8.7b)
breadboards: 1

parts:
  Part1 = Arduino Uno (Rev3)
  U1 = LCD-16X2 [package=lcd-8x2-kit]
  J1 = Piezo Speaker
  S1 = Pushbutton [package="[THT]"]
  S2 = Pushbutton [package="[THT]"]
  S3 = Pushbutton [package="[THT]"]
  R2 = Resistor [tolerance=±5% resistance=220 package=THT]
  R3 = Resistor [tolerance=±5% resistance=220 package=THT]
  R4 = Resistor [tolerance=±5% resistance=220 package=THT]

nets:
  N1: Part1.A0, S1.Pin_3, S2.Pin_3, S3.Pin_3, R4.Pin_0
  N2: Part1.D11_PWM/MOSI, U1.E
  N3: Part1.D12/MISO, U1.RS
  N4: Part1.D2, U1.DB7
  N5: Part1.D3_PWM, U1.DB6
  N6: Part1.D4, U1.DB5
  N7: Part1.D5_PWM, U1.DB4
  N8: Part1.D7, J1.pin2
  5V: Part1.5V, U1.VDD, S1.Pin_1, R2.Pin_1, R3.Pin_1
  GND: Part1.GND, U1.VSS, J1.pin1, R4.Pin_1
